# Fritzing sketch Schematic - LBB Light Sensor (saved by Fritzing 0.9.2b)

parts:
  Part2 = LightBlue Bean
  VCC2 = Battery
  Ligth_Sensor = Grove OLED 128x96

nets:
  VCC: Part2.VCC, Ligth_Sensor.VCC
  N1: Part2.AIN_A1, Ligth_Sensor.SCL
  N2: Part2.AIN_A0, Ligth_Sensor.SDA
  GND: Part2.GND, VCC2.-, Ligth_Sensor.GND
  N3: Part2.BAT, VCC2.+

notes:
  I2C Light Sensor From Adafruit
