# Fritzing sketch Schematic - LBB Soil Sensor (saved by Fritzing 0.9.2b)

parts:
  Part2 = LightBlue Bean
  VCC2 = Battery
  Soil_Sensor = Grove OLED 128x96
  C1 = Capacitor Polarized [package=panasonic_d]
  R1 = Resistor [tolerance=±5% resistance=470 package="2010 [SMD]"]

nets:
  N1: Part2.D5/SCK, R1.Pin_0
  N2: Part2.AIN_A1, Soil_Sensor.SCL
  N3: Part2.AIN_A0, Soil_Sensor.SDA
  N4: Part2.1, Soil_Sensor.VCC, R1.Pin_1
  GND: Part2.GND, VCC2.-, Soil_Sensor.GND, C1.+
  N5: Part2.BAT, VCC2.+, C1.-

notes:
  Chirp, an I2C Soil Sensor from Tindie
  Resistor at Pin 5 to Mitigate Inductance Spikes
