# Fritzing sketch Schematic - LBB Soil Sensor (saved by Fritzing 0.9.2b)

parts:
  Part2 = LightBlue Bean
  VCC2 = Battery
  Soil_Sensor = Grove OLED 128x96
  C1 = Capacitor Polarized [package=panasonic_d]

nets:
  VCC: Part2.VCC, Soil_Sensor.VCC
  N1: Part2.AIN_A1, Soil_Sensor.SCL
  N2: Part2.AIN_A0, Soil_Sensor.SDA
  GND: Part2.GND, VCC2.-, Soil_Sensor.GND, C1.+
  N3: Part2.BAT, VCC2.+, C1.-

notes:
  Chirp, an I2C Soil Sensor from Tindie
